# Fritzing sketch Reciever (saved by Fritzing 0.9.3b)

parts:
  Part2 = Arduino Mega 2560 (Rev3)
  J1 = Basic Servo
  J2 = Basic Servo
  J3 = Basic Servo
  M1 = DC Motor
  M2 = DC Motor
  M3 = DC Motor
  M4 = DC Motor
  S1 = H-Bridge with L298N
  KY-1 = Keyes Relay [package=THT]
  Part3 = NRF24L01+ Breakout Board

nets:
  N1: Part2.D13_PWM, KY-1.signal
  N2: Part2.D12_PWM, J3.pulse
  N3: Part2.D11_PWM, S1.ENA
  N4: Part2.D10_PWM, S1.IN2
  N5: Part2.D9_PWM, S1.IN1
  N6: Part2.D8_PWM, Part3.CS
  VCC: Part2.5V, J1.vcc, J2.vcc, J3.vcc, S1.5V, KY-1.power, Part3.VCC
  GND: Part2.GND, J1.gnd, J2.gnd, J3.gnd, S1.GND, KY-1.ground, Part3.GND
  N7: Part2.D2_PWM, J1.pulse
  N8: Part2.D3_PWM, J2.pulse
  N9: Part2.D4_PWM, S1.ENB
  N10: Part2.D5_PWM, S1.IN4
  N11: Part2.D6_PWM, S1.IN3
  N12: Part2.D7_PWM, Part3.CE
  N13: Part2.D50, Part3.MISO
  N14: Part2.D51, Part3.MOSI
  N15: Part2.D52, Part3.SCK
  N16: M1.pin_1, M2.pin_1, S1.M1-02
  N17: M1.pin_2, M2.pin_2, S1.M1-01
  N18: M3.pin_1, M4.pin_1, S1.M2-01
  N19: M3.pin_2, M4.pin_2, S1.M2-02

notes:
  12V

custom parts:
  H-Bridge with L298N: h-bridge
  Keyes Relay: The Keyes 5V relay module is suitable for SCM development, home appliance control. It uses a 5V~12V TIL control signal which can control DC / AC signal.
