# Fritzing sketch Transmiter (saved by Fritzing 0.9.3b)

parts:
  Mod1 = KY-023 Dual Axis Joystick Module [package="Breakout board"]
  Part1 = NRF24L01+ Breakout Board
  Part2 = Arduino Nano (Rev3.0)
  S1 = Pushbutton [package="[SMD]"]
  S2 = Pushbutton [package="[SMD]"]
  S3 = Pushbutton [package="[SMD]"]
  S4 = Pushbutton [package="[SMD]"]
  Mod2 = KY-023 Dual Axis Joystick Module [package="Breakout board"]
  S5 = Limit Switch [package="Breakout Board"]

nets:
  GND: Mod1.GND, Part1.GND, Part2.GND, S1.Pin_3, S1.Pin_4, S2.Pin_3, S2.Pin_4, S3.Pin_3, S3.Pin_4, S4.Pin_3, S4.Pin_4, Mod2.GND
  +5V: Mod1.+5V, Part1.VCC, Part2.5V, Mod2.+5V, S5.V
  N1: Mod1.VRx, Part2.A2
  N2: Part1.CE, Part2.D7
  N3: Part1.CS, Part2.D8
  N4: Part1.SCK, Part2.D13/SCK
  N5: Part1.MOSI, Part2.D12/MISO
  N6: Part1.MISO, Part2.D11/MOSI
  N7: Part2.D2, S4.Pin_1, S4.Pin_2
  N8: Part2.D3, S1.Pin_1, S1.Pin_2
  N9: Part2.D4, S3.Pin_1, S3.Pin_2
  N10: Part2.D5, S2.Pin_1, S2.Pin_2
  N11: Part2.D6, S5.S
  N12: Part2.A1, Mod2.VRy
  N13: Part2.A0, Mod2.VRx

custom parts:
  KY-023 Dual Axis Joystick Module: KY-023 Dual-Axis Joystick Module.
  Limit Switch: Generic limit switch commonly found on 3D printers. Typical lever microswitch mounted on a PCB board with a 3 pin JST XH connector.
